// Logisim project Lab1.circ as structural Verilog
module ROM (
);

  ROM_part rom_1 ();  // open: addr, data, sel
endmodule

module ROM_based_FSM (
  input  CE,
  input  OE
);

  wire clock_1_out;
  wire [2:0] Current_State_q;
  wire [5:0] rom_1_data;

  Clock clock_1 (.out(clock_1_out));
  Register #(.width(3), .trigger("falling")) Current_State (
    .D(rom_1_data[2:0]), .en(CE), .Q(Current_State_q), .clk(clock_1_out));  // open: clr
  LED O2 (.in(rom_1_data[5]));
  ROM_part #(.addrWidth(3), .dataWidth(6)) rom_1 (.addr(Current_State_q), .data(rom_1_data), .sel(OE));
  LED O1 (.in(rom_1_data[4]));
  LED O0 (.in(rom_1_data[3]));

  // Notes on the sheet:
  //   contents of rom_1 (hex, n*v repeats v):
  //   4 15 13 8 9 22
endmodule
