// Logisim project Lab2.circ as structural Verilog: 14 circuits, main circuit main
module main (
  input  [3:0] Op,
  output [31:0] R,
  output C,
  output V,
  output N,
  output Z
);

  ALU ALU (.X(32'h7fffffff), .Y(32'h7fffffff), .Op(Op), .R(R), .C(C), .V(V), .N(N), .Z(Z));
endmodule

module ALU (
  input  [31:0] X,
  input  [31:0] Y,
  input  [3:0] Op,
  output [31:0] R,
  output C,
  output V,
  output N,
  output Z
);

  wire [3:0] ADD_Flags, NEG_Flags, NOP_Flags, RY_Flags, SMIN_Flags, SUB_Flags, UMIN_Flags;
  wire [31:0] ADD_Out, NEG_Out, NOP_Out, RY_Out, SMIN_Out, SUB_Out, UMIN_Out;

  NOP NOP (.out_1(NOP_Out), .out_2(NOP_Flags[0]), .out_3(NOP_Flags[1]), .out_4(NOP_Flags[2]), .out_5(NOP_Flags[3]));
  ADD ADD (.X(X), .Y(Y), .X_Y(ADD_Out), .C(ADD_Flags[0]), .V(ADD_Flags[1]), .N(ADD_Flags[2]), .Z(ADD_Flags[3]));
  SUB SUB (.X(X), .Y(Y), .out_3(SUB_Out), .C(SUB_Flags[0]), .V(SUB_Flags[1]), .N(SUB_Flags[2]), .Z(SUB_Flags[3]));
  RY RY (.Y(Y), .Out(RY_Out), .C(RY_Flags[0]), .V(RY_Flags[1]), .N(RY_Flags[2]), .Z(RY_Flags[3]));
  NEG NEG (.Y(Y), ._2Comp(NEG_Out), .C(NEG_Flags[0]), .V(NEG_Flags[1]), .N(NEG_Flags[2]), .Z(NEG_Flags[3]));
  UMIN UMIN (
    .X(X), .Y(Y), .out_3(UMIN_Out), .C(UMIN_Flags[0]), .V(UMIN_Flags[1]), .N(UMIN_Flags[2]), .Z(UMIN_Flags[3]));
  SMIN SMIN (
    .X(X), .Y(Y), .out_3(SMIN_Out), .C(SMIN_Flags[0]), .V(SMIN_Flags[1]), .N(SMIN_Flags[2]), .Z(SMIN_Flags[3]));
  Multiplexer #(.select(4), .width(32)) multiplexer_1 (
    .in0(NOP_Out), .in1(ADD_Out), .in2(SUB_Out), .in3(RY_Out), .in9(UMIN_Out), .in10(SMIN_Out),
    .in14(NEG_Out), .out(R), .sel(Op));  // open: in4, in5, in6, in7, in8, in11, in12, in13, in15, en
  Multiplexer #(.select(4), .width(4)) multiplexer_2 (
    .in0(NOP_Flags), .in1(ADD_Flags), .in2(SUB_Flags), .in3(RY_Flags), .in9(UMIN_Flags), .in10(SMIN_Flags),
    .in14(NEG_Flags), .out({Z, N, V, C}), .sel(Op));  // open: in4, in5, in6, in7, in8, in11, in12, in13, in15, en
endmodule

module NOP (
  output [31:0] out_1,
  output out_2,
  output out_3,
  output out_4,
  output out_5
);


  assign out_1 = {32{1'b0}};
  assign out_2 = 1'b0;
  assign out_3 = 1'b0;
  assign out_4 = 1'b0;
  assign out_5 = 1'b0;
endmodule

module ADD (
  input  [31:0] X,
  input  [31:0] Y,
  output [31:0] X_Y,
  output C,
  output V,
  output N,
  output Z
);

  Adder #(.width(32)) adder_1 (.a(X), .b(Y), .out(X_Y), .cout(C));  // open: cin
  CheckOverflow checkoverflow_1 (.MSB_R(X_Y[31]), .MSB_X(X[31]), .MSB_Y(Y[31]), .V(V));
  CheckNegative checknegative_1 (.In(X_Y), .isNegative(N));
  CheckZero checkzero_1 (.In(X_Y), .isZero(Z));

  // Other names for the same wires on the sheet: X_MSB = X[31]; Y_MSB = Y[31]
endmodule

module SUB (
  input  [31:0] X,
  input  [31:0] Y,
  output [31:0] out_3,
  output C,
  output V,
  output N,
  output Z
);

  wire [31:0] n2scomplement_1__2comp;

  _2sComplement u_2scomplement_1 (.Y(Y), ._2Comp(n2scomplement_1__2comp));  // open: C, V, N, Z
  ADD add_1 (.X(X), .Y(n2scomplement_1__2comp), .X_Y(out_3), .C(C), .V(V), .N(N), .Z(Z));
endmodule

module RY (
  input  [31:0] Y,
  output [31:0] Out,
  output C,
  output V,
  output N,
  output Z
);

  CheckNegative CN (.In(Y), .isNegative(N));
  CheckZero CZ (.In(Y), .isZero(Z));

  assign C = 1'b0;
  assign Out = Y;
  assign V = 1'b0;
endmodule

module NEG (
  input  [31:0] Y,
  output [31:0] _2Comp,
  output C,
  output V,
  output N,
  output Z
);

  wire [31:0] not_1_out;

  assign not_1_out = ~Y;  // NOT_Gate not_1, 32 bits wide
  ADD add_1 (.X(not_1_out), .Y(32'h1), .X_Y(_2Comp), .C(C), .N(N), .Z(Z));  // open: V
  CheckOverflow checkoverflow_1 (.MSB_R(_2Comp[31]), .MSB_X(Y[31]), .MSB_Y(Y[31]), .V(V));
endmodule

module UMIN (
  input  [31:0] X,
  input  [31:0] Y,
  output [31:0] out_3,
  output C,
  output V,
  output N,
  output Z
);

  wire comparator_1_gt;

  Comparator #(.width(32), .mode("unsigned")) comparator_1 (.a(X), .b(Y), .gt(comparator_1_gt));  // open: eq, lt
  Multiplexer #(.width(32)) multiplexer_1 (.in0(X), .in1(Y), .out(out_3), .sel(comparator_1_gt));  // open: en
  CheckNegative checknegative_1 (.In(out_3), .isNegative(N));
  CheckZero checkzero_1 (.In(out_3), .isZero(Z));

  assign C = 1'b0;
  assign V = 1'b0;
endmodule

module SMIN (
  input  [31:0] X,
  input  [31:0] Y,
  output [31:0] out_3,
  output C,
  output V,
  output N,
  output Z
);

  wire comparator_1_gt;

  Comparator #(.width(32)) comparator_1 (.a(X), .b(Y), .gt(comparator_1_gt));  // open: eq, lt
  Multiplexer #(.width(32)) multiplexer_1 (.in0(X), .in1(Y), .out(out_3), .sel(comparator_1_gt));  // open: en
  CheckNegative checknegative_1 (.In(out_3), .isNegative(N));
  CheckZero checkzero_1 (.In(out_3), .isZero(Z));

  assign C = 1'b0;
  assign V = 1'b0;
endmodule

module CheckOverflow (
  input  MSB_R,
  input  MSB_X,
  input  MSB_Y,
  output V
);

  wire and_1_out, and_2_out, not_1_out, not_2_out, not_3_out;

  not not_1 (not_1_out, MSB_X);
  not not_2 (not_2_out, MSB_Y);
  not not_3 (not_3_out, MSB_R);
  and and_1 (and_1_out, MSB_R, not_1_out, not_2_out);
  and and_2 (and_2_out, not_3_out, MSB_X, MSB_Y);
  or or_1 (V, and_1_out, and_2_out);
endmodule

module CheckZero (
  input  [31:0] In,
  output isZero
);

  Comparator #(.width(32), .mode("unsigned")) comparator_1 (.a(In), .b({32{1'b0}}), .eq(isZero));  // open: gt, lt
endmodule

module CheckNegative (
  input  [31:0] In,
  output isNegative
);


  assign isNegative = In[31];
endmodule

module _2sComplement (
  input  [31:0] Y,
  output [31:0] _2Comp,
  output C,
  output V,
  output N,
  output Z
);

  wire [31:0] not_1_out;

  assign not_1_out = ~Y;  // NOT_Gate not_1, 32 bits wide
  ADD add_1 (.X(not_1_out), .Y(32'h1), .X_Y(_2Comp), .C(C), .V(V), .N(N), .Z(Z));
endmodule

module Tunnel_Test (
  input  in_1,
  input  in_2,
  input  in_3,
  input  in_4,
  input  [7:0] in_5,
  input  [7:0] in_6,
  output out_7,
  output out_8,
  output [7:0] out_9,
  output out_10,
  output [7:0] out_11,
  output out_12,
  output out_13,
  output out_14,
  output out_15
);

  wire not_1_out;

  Adder adder_1 (.a(in_5), .b(in_6), .out(out_9), .cout(out_10));  // open: cin
  assign out_8 = not_1_out ? in_2 : 1'bz;  // Controlled_Buffer controlled_buffer_1
  not not_1 (not_1_out, in_4);
  Subtractor subtractor_1 (.a(in_5), .b(in_6), .out(out_11), .bout(out_12));  // open: bin
  Comparator comparator_1 (.a(in_6), .b(in_5), .gt(out_13), .eq(out_14), .lt(out_15));
  assign out_8 = in_4 ? in_3 : 1'bz;  // Controlled_Buffer controlled_buffer_2
  _2sComplement u_2scomplement_1 ();  // open: Y, _2Comp, C, V, N, Z
  Adder adder_2 ();  // open: a, b, out, cin, cout

  assign out_7 = in_1;

  // Other names for the same wires on the sheet: A = in_1
endmodule
