// Logisim project Lab3Part1.circ as structural Verilog: 1 circuit, main circuit main
module main (
);

  // ALU alu_1: pin names not known
  RAM #(.addrWidth(4), .dataWidth(32)) ram_1 ();  // open: addr, data, sel, clk, ld, clr
  ROM #(.addrWidth(2), .dataWidth(32)) rom_1 ();  // open: addr, data, sel
  Register #(.width(2)) register_1 ();  // open: D, en, Q, clk, clr
  T_Flip_Flop Toggle_Switch ();  // open: clk, T, Q, Qn, preset, reset, en
  Button button_1 ();  // open: out
  // Reg32 reg32_1: pin names not known
  // Reg32 reg32_2: pin names not known
endmodule
