// Logisim project Lab3Part1.circ as structural Verilog
module Simple_Processing_Circuit (
);

  wire alu_1_p1, Clk, not_1_out, reg32_1_p7, T1CE, T1OE, T2CE, T2OE, WordR, WordW;
  wire [3:0] Addr, OPR;
  wire [31:0] ram_1_data, reg32_1_p4, reg32_2_p5;

  Control_FSM control_fsm_1 (
    .Clk(Clk), .Addr(Addr), .WordR(WordR), .WordW(WordW), .T1CE(T1CE), .T1OE(T1OE), .OPR(OPR), .T2CE(T2CE),
    .T2OE(T2OE));
  // ALU alu_1: pin names not known; wires that end beside it: alu_1_p1
  not not_1 (not_1_out, Clk);
  // Reg32 reg32_1: pin names not known; wires that end beside it: OPR, T1CE, T1OE, reg32_1_p4, Clk, reg32_1_p4, reg32_1_p7, reg32_1_p7
  // Reg32 reg32_2: pin names not known; wires that end beside it: T2CE, T2OE, Clk, alu_1_p1, reg32_2_p5
  RAM #(.addrWidth(4), .dataWidth(32)) ram_1 (
    .addr(Addr), .data(ram_1_data), .sel(1'b1), .clk(not_1_out), .ld(WordR));  // open: clr
  assign reg32_1_p4 = WordR ? ram_1_data : 32'bz;  // Controlled_Buffer controlled_buffer_1
  assign ram_1_data = WordW ? reg32_2_p5 : 32'bz;  // Controlled_Buffer controlled_buffer_2
  Clock clock_1 (.out(Clk));
endmodule

module Control_FSM (
  input  Clk,
  output [3:0] Addr,
  output [3:0] OPR,
  output WordR,
  output WordW,
  output T1CE,
  output T1OE,
  output T2CE,
  output T2OE
);

  wire [4:0] register_1_q, rom_1_data;

  Register #(.width(5)) register_1 (.D(rom_1_data), .Q(register_1_q), .clk(Clk));  // open: en, clr
  ROM #(.addrWidth(5), .dataWidth(19)) rom_1 (
    .addr(register_1_q), .data({Addr, OPR, WordR, WordW, T1CE, T1OE, T2CE, T2OE, rom_1_data}));  // open: sel

  // Notes on the sheet:
  //   contents of rom_1 (hex, n*v repeats v):
  //   8501 10cc2 18220
endmodule

module _32_bit_Data_Bus (
  input  RAM,
  input  WordR,
  input  WordW,
  input  T2,
  output ALU
);
endmodule

module Simple_Processing_Circuit_2 (
);

  wire alu_1_p1, Clk, not_1_out, reg32_1_p7, T1CE, T1OE, T2CE, T2OE, WordR, WordW;
  wire [3:0] Addr, OPR;
  wire [31:0] ram_1_data, reg32_1_p4, reg32_2_p5;

  Control_FSM control_fsm_1 (
    .Clk(Clk), .Addr(Addr), .WordR(WordR), .WordW(WordW), .T1CE(T1CE), .T1OE(T1OE), .OPR(OPR), .T2CE(T2CE),
    .T2OE(T2OE));
  // ALU alu_1: pin names not known; wires that end beside it: alu_1_p1
  not not_1 (not_1_out, Clk);
  // Reg32 reg32_1: pin names not known; wires that end beside it: OPR, T1CE, T1OE, reg32_1_p4, Clk, reg32_1_p4, reg32_1_p7, reg32_1_p7
  // Reg32 reg32_2: pin names not known; wires that end beside it: T2CE, T2OE, Clk, alu_1_p1, reg32_2_p5
  RAM #(.addrWidth(4), .dataWidth(32)) ram_1 (
    .addr(Addr), .data(ram_1_data), .sel(1'b1), .clk(not_1_out), .ld(WordR));  // open: clr
  assign reg32_1_p4 = WordR ? ram_1_data : 32'bz;  // Controlled_Buffer controlled_buffer_1
  assign ram_1_data = WordW ? reg32_2_p5 : 32'bz;  // Controlled_Buffer controlled_buffer_2
  Clock clock_1 (.out(Clk));
endmodule

// a
module Given_Components (
);

  // ALU alu_1: pin names not known
  RAM #(.addrWidth(4), .dataWidth(32)) ram_1 ();  // open: addr, data, sel, clk, ld, clr
  ROM #(.addrWidth(2), .dataWidth(32)) rom_1 ();  // open: addr, data, sel
  Register #(.width(2)) register_1 ();  // open: D, en, Q, clk, clr
  Button button_1 ();  // open: out
  T_Flip_Flop Toggle_Switch ();  // open: clk, T, Q, Qn, preset, reset, en
  // Reg32 reg32_1: pin names not known
  // Reg32 reg32_2: pin names not known
endmodule

module Control_FSM_2 (
  input  Clk,
  output [3:0] Addr,
  output [3:0] OPR,
  output WordR,
  output WordW,
  output T1CE,
  output T1OE,
  output T2CE,
  output T2OE
);

  wire [4:0] register_1_q, rom_1_data;

  Register #(.width(5)) register_1 (.D(rom_1_data), .Q(register_1_q), .clk(Clk));  // open: en, clr
  ROM #(.addrWidth(5), .dataWidth(19)) rom_1 (
    .addr(register_1_q), .data({Addr, OPR, WordR, WordW, T1CE, T1OE, T2CE, T2OE, rom_1_data}));  // open: sel

  // Notes on the sheet:
  //   contents of rom_1 (hex, n*v repeats v):
  //   8501 10cc2 18220
endmodule
