// Logisim project Lab3Part1_Benni.circ as structural Verilog: 2 circuits, main circuit main
module main (
);

  // ALU alu_1: pin names not known
  RAM #(.addrWidth(4), .dataWidth(32)) ram_1 ();  // open: addr, data, sel, clk, ld, clr
  ROM #(.addrWidth(2), .dataWidth(32)) rom_1 ();  // open: addr, data, sel
  Register #(.width(2)) register_1 ();  // open: D, en, Q, clk, clr
  T_Flip_Flop Toggle_Switch ();  // open: clk, T, Q, Qn, preset, reset, en
  Button button_1 ();  // open: out
  // Reg32 reg32_1: pin names not known
  // Reg32 reg32_2: pin names not known
endmodule

module Processing_unit (
  input  CLK,
  output OUTPUT,
  output out_3,
  output out_4,
  output out_5
);

  wire alu_1_p1, CLEAR, CLK_t, not_1_out, or_1_out, reg32_1_p5, T1CE, T1OE, T2CE, T2OE, WordR, WordW;
  wire [1:0] register_1_q, rom_1_data;
  wire [3:0] ADDRESS, OPERTION;
  wire [31:0] DATA_BUS;

  Button button_1 (.out(CLEAR));
  D_Flip_Flop d_ff_1 (.Q(CLK_t));  // open: clk, D, Qn, preset, en, reset
  Register #(.width(2)) register_1 (.D(rom_1_data), .Q(register_1_q), .clk(CLK));  // open: en, clr
  ROM #(.addrWidth(2), .dataWidth(16)) rom_1 (
    .addr(register_1_q), .data({OPERTION, ADDRESS, WordR, WordW, T1CE, T1OE, T2CE, T2OE, rom_1_data}));  // open: sel
  not not_1 (not_1_out, CLK_t);
  or or_1 (or_1_out, WordW, WordR);
  // Reg32 reg32_1: pin names not known; wires that end beside it: CLK_t, DATA_BUS, T1CE, T1OE, reg32_1_p5, CLEAR, reg32_1_p5, DATA_BUS, OPERTION
  RAM #(.addrWidth(4), .dataWidth(32)) ram_1 (
    .addr(ADDRESS), .data(DATA_BUS), .sel(or_1_out), .clk(not_1_out), .ld(WordR), .clr(CLEAR));
  // ALU alu_1: pin names not known; wires that end beside it: alu_1_p1, OUTPUT, out_3, out_4, out_5, CLK_t, alu_1_p1
  // Reg32 reg32_2: pin names not known; wires that end beside it: T2CE, T2OE, DATA_BUS, CLEAR

  // Other names for the same wires on the sheet: C = OUTPUT; N = out_4; V = out_3; Z = out_5

  // Notes on the sheet:
  //   INPUT
  //   contents of rom_1 (hex, n*v repeats v):
  //   8501 cc2 8220
endmodule
