// Logisim project Lab3Part2.circ as structural Verilog
module Simple_Processing_Circuit (
  input  [3:0] Opcode,
  input  [3:0] DWord,
  input  [3:0] SXWord,
  input  [3:0] SYWord
);

  wire alu_1_p1, Clk, not_1_out, not_2_out, reg32_1_p7, T1CE, T1OE, T2CE, T2OE, WordR, WordW;
  wire [3:0] Addr, OPR;
  wire [15:0] n16_bit_instruction_register_1_instructions;
  wire [31:0] ram_1_data, reg32_1_p4, reg32_2_p5;

  Control_FSM control_fsm_1 (
    .Clk(Clk), .IR(n16_bit_instruction_register_1_instructions), .OPR(OPR), .Address(Addr), .WordR(WordR),
    .T1OE(T1OE), .T1CE(T1CE), .WordW(WordW), .T2CE(T2CE), .T2OE(T2OE));
  _16_bit_Instruction_Register u_16_bit_instruction_register_1 (
    .Opcode_in(Opcode), .DWord_in(DWord), .SXWord_in(SXWord), .SYWord_in(SYWord), .Clk(not_1_out),
    .Instructions(n16_bit_instruction_register_1_instructions));
  not not_1 (not_1_out, Clk);
  // ALU alu_1: pin names not known; wires that end beside it: alu_1_p1
  Clock clock_1 (.out(Clk));
  not not_2 (not_2_out, Clk);
  // Reg32 reg32_1: pin names not known; wires that end beside it: OPR, T1CE, T1OE, reg32_1_p4, Clk, reg32_1_p4, reg32_1_p7, reg32_1_p7
  // Reg32 reg32_2: pin names not known; wires that end beside it: T2CE, T2OE, Clk, alu_1_p1, reg32_2_p5
  RAM #(.addrWidth(4), .dataWidth(32)) ram_1 (
    .addr(Addr), .data(ram_1_data), .sel(1'b1), .clk(not_2_out), .ld(WordR));  // open: clr
  assign reg32_1_p4 = WordR ? ram_1_data : 32'bz;  // Controlled_Buffer controlled_buffer_1
  assign ram_1_data = WordW ? reg32_2_p5 : 32'bz;  // Controlled_Buffer controlled_buffer_2
endmodule

// Instruction Register
module _16_bit_Instruction_Register (
  input  [3:0] Opcode_in,
  input  [3:0] DWord_in,
  input  [3:0] SXWord_in,
  input  [3:0] SYWord_in,
  input  Clk,
  output [15:0] Instructions
);

  Register #(.width(16)) register_1 (
    .D({Opcode_in, DWord_in, SXWord_in, SYWord_in}), .Q(Instructions), .clk(Clk));  // open: en, clr
endmodule

module Control_FSM (
  input  Clk,
  input  [15:0] IR,
  output T2OE,
  output T2CE,
  output T1OE,
  output T1CE,
  output WordW,
  output WordR,
  output [3:0] Address,
  output [3:0] OPR
);

  wire ANOP, AOP, DR, One_Source_Op, SXR, SYR;
  wire [1:0] Next_State_next_state, register_1_q;
  wire [3:0] rom_1_data;

  assign OPR = ANOP ? 4'b0000 : 4'bz;  // Controlled_Buffer controlled_buffer_1
  One_Source_Op u_One_Source_Op (.Opcode(IR[15:12]), .OneSourceOp(One_Source_Op));
  Register #(.width(2)) register_1 (.D(Next_State_next_state), .Q(register_1_q), .clk(Clk));  // open: en, clr
  assign OPR = AOP ? IR[15:12] : 4'bz;  // Controlled_Buffer controlled_buffer_2
  assign Address = DR ? IR[11:8] : 4'bz;  // Controlled_Buffer controlled_buffer_3
  ROM #(.addrWidth(2), .dataWidth(4)) rom_1 (.addr(register_1_q), .data(rom_1_data));  // open: sel
  assign Address = SXR ? IR[7:4] : 4'bz;  // Controlled_Buffer controlled_buffer_4
  assign Address = SYR ? IR[3:0] : 4'bz;  // Controlled_Buffer controlled_buffer_5
  FSM_Output_Signals Output_Signals (
    .Current_State(rom_1_data[3:2]),
    .FSM_Outputs({AOP, ANOP, DR, SXR, SYR, WordR, WordW, T1CE, T1OE, T2CE, T2OE}));
  Decode_Next_State Next_State (
    .CS(rom_1_data[3:2]), .NS(rom_1_data[1:0]), .OneSourceOp(One_Source_Op),
    .Next_State(Next_State_next_state));

  // Notes on the sheet:
  //   contents of rom_1 (hex, n*v repeats v):
  //   1 6 b f
endmodule

module Decode_Next_State (
  input  [1:0] CS,
  input  [1:0] NS,
  input  OneSourceOp,
  output [1:0] Next_State
);

  wire isEqual, not_1_out;
  wire [1:0] multiplexer_1_out;

  Multiplexer #(.width(2)) multiplexer_1 (
    .in0(2'b00), .in1(2'b01), .out(multiplexer_1_out), .sel(OneSourceOp));  // open: en
  assign Next_State = not_1_out ? NS : 2'bz;  // Controlled_Buffer controlled_buffer_1
  not not_1 (not_1_out, isEqual);
  assign Next_State = isEqual ? multiplexer_1_out : 2'bz;  // Controlled_Buffer controlled_buffer_2
  Comparator #(.width(2), .mode("unsigned")) comparator_1 (.a(CS), .b(NS), .eq(isEqual));  // open: gt, lt

  // Other names for the same wires on the sheet: OSP = OneSourceOp
endmodule

module One_Source_Op (
  input  [3:0] Opcode,
  output OneSourceOp
);

  wire not_1_out;

  and and_1 (OneSourceOp, Opcode[0], Opcode[1], not_1_out);
  not not_1 (not_1_out, Opcode[3]);
endmodule

module FSM_Output_Signals (
  input  [1:0] Current_State,
  output [10:0] FSM_Outputs
);

  Multiplexer #(.select(2), .width(11)) multiplexer_1 (
    .in0(11'h2a8), .in1(11'h466), .in2(11'h311), .in3(11'h200), .out(FSM_Outputs), .sel(Current_State));  // open: en
endmodule

module Given_Components (
);

  // ALU alu_1: pin names not known
  RAM #(.addrWidth(4), .dataWidth(32)) ram_1 ();  // open: addr, data, sel, clk, ld, clr
  ROM #(.addrWidth(2), .dataWidth(32)) rom_1 ();  // open: addr, data, sel
  Register #(.width(2)) register_1 ();  // open: D, en, Q, clk, clr
  Button button_1 ();  // open: out
  T_Flip_Flop Toggle_Switch ();  // open: clk, T, Q, Qn, preset, reset, en
  // Reg32 reg32_1: pin names not known
  // Reg32 reg32_2: pin names not known
endmodule
