// Logisim project Lab6.circ as structural Verilog: 7 circuits, main circuit Given Components
module Main_Memory (
);

  wire and_1_out, IBRead, IBWrite, Inverted_Clock, nor_1_out, or_1_out;
  wire [31:0] InterconnectionAddressBus, InterconnectionDataBus;

  nor nor_1 (nor_1_out, InterconnectionAddressBus[6], InterconnectionAddressBus[7], InterconnectionAddressBus[8], InterconnectionAddressBus[9], InterconnectionAddressBus[10], InterconnectionAddressBus[11], InterconnectionAddressBus[12], InterconnectionAddressBus[13], InterconnectionAddressBus[14], InterconnectionAddressBus[15], InterconnectionAddressBus[16], InterconnectionAddressBus[17], InterconnectionAddressBus[18], InterconnectionAddressBus[19], InterconnectionAddressBus[20], InterconnectionAddressBus[21], InterconnectionAddressBus[22], InterconnectionAddressBus[23], InterconnectionAddressBus[24], InterconnectionAddressBus[25], InterconnectionAddressBus[26], InterconnectionAddressBus[27], InterconnectionAddressBus[28], InterconnectionAddressBus[29], InterconnectionAddressBus[30], InterconnectionAddressBus[31]);
  and and_1 (and_1_out, nor_1_out, or_1_out);
  or or_1 (or_1_out, IBWrite, IBRead);
  RAM #(.addrWidth(6), .dataWidth(32)) ram_1 (
    .addr(InterconnectionAddressBus[5:0]), .data(InterconnectionDataBus), .sel(and_1_out),
    .clk(Inverted_Clock), .ld(IBRead));  // open: clr

  // Notes on the sheet:
  //   Use this Main Memory component 
  //   in Part 2 ONLY!
endmodule

module Processor_and_Main_Memory (
);

  wire alu_1_p1, alu_1_p2, alu_1_p3, alu_1_p4, alu_1_p5, and_1_out, C1OE, Clock, CLR, control_fsm_1_irce,
       IBRead, IBWrite, Inverted_Clock, nor_1_out, or_1_out, PCOE, RegLD, RegSEL, T1_p7, T1CE, T1OE, T2_p6,
       T2CE, T2OE;
  wire [3:0] control_fsm_1_regaddr, Opr;
  wire [5:0] IBI_Flags, interconnection_bus_interface_1_mar_out;
  wire [7:0] control_fsm_1_current_state;
  wire [31:0] control_fsm_1_const_operand, instruction_register_1_instructions,
       interconnection_bus_interface_1_reg_to_mem_out;
  wire [31:6] interconnection_bus_interface_1_mar_out_2;

  Clock Testing_clock (.out(Clock));
  not not_1 (Inverted_Clock, Clock);
  // Probe on control_fsm_1_current_state
  Instruction_Register instruction_register_1 (
    .Data(control_fsm_1_const_operand), .Clk(Clock), .Instructions(instruction_register_1_instructions),
    .IRCE(control_fsm_1_irce));
  Control_FSM control_fsm_1 (
    .Clk(Clock), .T2OE(T2OE), .T2CE(T2CE), .T1OE(T1OE), .T1CE(T1CE), .RegLD(RegLD), .RegSEL(RegSEL),
    .RegAddr(control_fsm_1_regaddr), .Opr(Opr), .C1OE(C1OE), .PCOE(PCOE), .IBI_Flags(IBI_Flags),
    .IBRead(IBRead), .IBWrite(IBWrite), .IRCE(control_fsm_1_irce),
    .Instructions(instruction_register_1_instructions), .Current_State(control_fsm_1_current_state),
    .Const_Operand(control_fsm_1_const_operand));
  // Probe on control_fsm_1_const_operand
  LED led_1 (.in(alu_1_p3));
  LED led_2 (.in(alu_1_p4));
  LED led_3 (.in(alu_1_p1));
  LED led_4 (.in(alu_1_p2));
  Button Press_to_Clear_Internal_Processor_State (.out(CLR));
  // Probe on control_fsm_1_regaddr
  assign control_fsm_1_regaddr = PCOE ? 4'b1111 : 4'bz;  // Controlled_Buffer PC_Addrs
  // Reg32 T1: pin names not known; wires that end beside it: Opr, T1CE, T1OE, control_fsm_1_const_operand, Clock, control_fsm_1_const_operand, T1_p7, T1_p7
  // ALU alu_1: pin names not known; wires that end beside it: alu_1_p1, alu_1_p2, alu_1_p3, alu_1_p4, alu_1_p5
  // Reg32 T2: pin names not known; wires that end beside it: T2CE, T2OE, Clock, alu_1_p5, control_fsm_1_const_operand, T2_p6
  assign control_fsm_1_const_operand = C1OE ? 32'h1 : 32'bz;  // Controlled_Buffer Const_1
  // Probe on control_fsm_1_regaddr
  // Probe on T2_p6
  Interconnection_Bus_Interface interconnection_bus_interface_1 (
    .Clk(Clock), .IBWrite(IBWrite), .IBRead(IBRead), .MAR_in(control_fsm_1_const_operand),
    .MAR_out({interconnection_bus_interface_1_mar_out_2, interconnection_bus_interface_1_mar_out}),
    .Reg_to_Mem_in(control_fsm_1_const_operand),
    .Reg_to_Mem_out(interconnection_bus_interface_1_reg_to_mem_out),
    .Mem_to_Reg_in(interconnection_bus_interface_1_reg_to_mem_out),
    .Mem_to_Reg_out(control_fsm_1_const_operand), .IBI_Flags(IBI_Flags));
  RAM #(.addrWidth(4), .dataWidth(32)) ram_1 (
    .addr(control_fsm_1_regaddr), .data(control_fsm_1_const_operand), .sel(RegSEL), .clk(Inverted_Clock),
    .ld(RegLD), .clr(CLR));
  // Probe on control_fsm_1_const_operand
  // Probe on {interconnection_bus_interface_1_mar_out_2, interconnection_bus_interface_1_mar_out}
  // Probe on interconnection_bus_interface_1_reg_to_mem_out
  nor nor_1 (nor_1_out, interconnection_bus_interface_1_mar_out_2[6], interconnection_bus_interface_1_mar_out_2[7], interconnection_bus_interface_1_mar_out_2[8], interconnection_bus_interface_1_mar_out_2[9], interconnection_bus_interface_1_mar_out_2[10], interconnection_bus_interface_1_mar_out_2[11], interconnection_bus_interface_1_mar_out_2[12], interconnection_bus_interface_1_mar_out_2[13], interconnection_bus_interface_1_mar_out_2[14], interconnection_bus_interface_1_mar_out_2[15], interconnection_bus_interface_1_mar_out_2[16], interconnection_bus_interface_1_mar_out_2[17], interconnection_bus_interface_1_mar_out_2[18], interconnection_bus_interface_1_mar_out_2[19], interconnection_bus_interface_1_mar_out_2[20], interconnection_bus_interface_1_mar_out_2[21], interconnection_bus_interface_1_mar_out_2[22], interconnection_bus_interface_1_mar_out_2[23], interconnection_bus_interface_1_mar_out_2[24], interconnection_bus_interface_1_mar_out_2[25], interconnection_bus_interface_1_mar_out_2[26], interconnection_bus_interface_1_mar_out_2[27], interconnection_bus_interface_1_mar_out_2[28], interconnection_bus_interface_1_mar_out_2[29], interconnection_bus_interface_1_mar_out_2[30], interconnection_bus_interface_1_mar_out_2[31]);
  and and_1 (and_1_out, nor_1_out, or_1_out);
  or or_1 (or_1_out, IBWrite, IBRead);
  RAM #(.addrWidth(6), .dataWidth(32)) ram_2 (
    .addr(interconnection_bus_interface_1_mar_out), .data(interconnection_bus_interface_1_reg_to_mem_out),
    .sel(and_1_out), .clk(Inverted_Clock), .ld(IBRead));  // open: clr

  // Notes on the sheet:
  //   (Poke to toggle)
  //   Invert for latching if needed
  //   (Does not clear ROM contents)
  //   16 x 32-bit Register Bank
  //   in Part 2 ONLY!
  //   Use this Main Memory component 
endmodule

module Control_FSM (
  input  Clk,
  input  [31:0] Instructions,
  output [7:0] Current_State,
  output T2OE,
  output T2CE,
  output T1OE,
  output T1CE,
  output RegLD,
  output RegSEL,
  output C1OE,
  output PCOE,
  output [5:0] IBI_Flags,
  output [3:0] RegAddr,
  output IBRead,
  output [3:0] Opr,
  output IBWrite,
  output IRCE,
  output [31:0] Const_Operand
);

  wire AADD, and_1_out, ANOP, AOP, CLR, DR, IRS16, IRS20, IRU16, IRU20, SXR, SYR;
  wire [7:0] multiplexer_1_out, NextState, rom_1_data;
  wire [31:31] rom_2_data;

  // Probe on Instructions[31:24]
  and and_1 (and_1_out, Current_State[0], Current_State[1], ~Current_State[2], ~Current_State[3], ~Current_State[4], ~Current_State[5], ~Current_State[6], ~Current_State[7]);  // AND_Gate
  ROM rom_1 (.addr(Instructions[31:24]), .data(rom_1_data), .sel(and_1_out));
  Multiplexer #(.width(8)) multiplexer_1 (
    .in0(NextState), .in1(rom_1_data), .out(multiplexer_1_out), .sel(and_1_out));  // open: en
  // Probe on multiplexer_1_out
  assign Const_Operand = IRU16 ? {{16{1'b0}}, Instructions[15:0]} : 32'bz;  // Controlled_Buffer controlled_buffer_1
  assign Const_Operand = IRU20 ? {{12{1'b0}}, Instructions[19:0]} : 32'bz;  // Controlled_Buffer controlled_buffer_2
  Register u_Current_State (.D(multiplexer_1_out), .Q(Current_State), .clk(Clk), .clr(CLR));  // open: en
  assign RegAddr = SYR ? Instructions[15:12] : 4'bz;  // Controlled_Buffer controlled_buffer_3
  assign RegAddr = SXR ? Instructions[19:16] : 4'bz;  // Controlled_Buffer controlled_buffer_4
  assign RegAddr = DR ? Instructions[23:20] : 4'bz;  // Controlled_Buffer controlled_buffer_5
  assign Opr = AOP ? Instructions[27:24] : 4'bz;  // Controlled_Buffer controlled_buffer_6
  // Probe on NextState
  ROM #(.dataWidth(32)) rom_2 (
    .addr(Current_State),
    .data({rom_2_data[31], AADD, IRCE, IBWrite, IBRead, IBI_Flags, PCOE, C1OE, AOP, ANOP, DR, SXR, SYR, RegSEL, RegLD, T1CE, T1OE, T2CE, T2OE, NextState}));  // open: sel
  ROM #(.dataWidth(4)) rom_3 (.addr(Current_State), .data({IRS20, IRS16, IRU20, IRU16}));  // open: sel
  assign Opr = ANOP ? 4'b0000 : 4'bz;  // Controlled_Buffer controlled_buffer_7
  assign Opr = AADD ? 4'b0001 : 4'bz;  // Controlled_Buffer controlled_buffer_8
  assign Const_Operand = IRS16 ? {{17{Instructions[15]}}, Instructions[14:0]} : 32'bz;  // Controlled_Buffer controlled_buffer_9
  assign Const_Operand = IRS20 ? {{13{Instructions[19]}}, Instructions[18:0]} : 32'bz;  // Controlled_Buffer controlled_buffer_10

  // Other names for the same wires on the sheet: IR16[15:0] = Instructions[15:0]; IR20[19:0] = Instructions[19:0];
  //   Clock = Clk; MARCE = IBI_Flags[0]; MAROE = IBI_Flags[1]; MDRCE = IBI_Flags[2]; MDROE = IBI_Flags[3];
  //   MDRput = IBI_Flags[4]; MDRget = IBI_Flags[5]; opcode[7:0] = Instructions[31:24];
  //   InternalDataBus[31:0] = Const_Operand

  // Notes on the sheet:
  //   Decode ROM
  //   Use opcode to pick next state during decode state
  //   For each instruction, this ROM holds the next state that follows the Decode State.
  //   This design requies that Decode state is state  0x03
  //   contents of rom_1 (hex, n*v repeats v):
  //   0 4 4 7 4 4 4 7 15*0 b 9*0 8 8 a 8 8 8 a 8*0 e 14 0 0 11 17
  //   Constant 0
  //   upper 4 bits of opcode
  //   not used in this lab
  //   next state from Output ROM
  //   Control FSM Outputs
  //   Control FSM (HI ROM)
  //   contents of rom_2 (hex, n*v repeats v):
  //   323801 48c80602 25020003 122100 2b805 47606 32100 47206 2b809 40606 40206 5320c a080d 40000706
  //   22b00f 8c20010 5032000 22b012 2833013 11420000 2b815 40616 22010f 2b818 40000619 220112
  //   contents of rom_3 (hex, n*v repeats v):
  //   9*0 1 2 10*0 4 0 0 4
  //   Register Address Bus
endmodule

module Instruction_Register (
  input  [31:0] Data,
  input  IRCE,
  input  Clk,
  output [31:0] Instructions
);

  wire not_1_out;

  not not_1 (not_1_out, Clk);
  Register #(.width(32)) Instruction_Register (.D(Data), .en(IRCE), .Q(Instructions), .clk(not_1_out));  // open: clr
endmodule

module Interconnection_Bus_Interface (
  input  Clk,
  input  [5:0] IBI_Flags,
  input  [31:0] Reg_to_Mem_in,
  input  [31:0] MAR_in,
  input  IBRead,
  input  IBWrite,
  input  [31:0] Mem_to_Reg_in,
  output [31:0] Mem_to_Reg_out,
  output [31:0] MAR_out,
  output [31:0] Reg_to_Mem_out
);

  wire [31:0] MDR_p4, MDR_p5;

  // Reg32 MDR: pin names not known; wires that end beside it: IBI_Flags[2], IBI_Flags[3], Clk, MDR_p4, MDR_p5
  assign MDR_p4 = IBI_Flags[4] ? Reg_to_Mem_in : 32'bz;  // Controlled_Buffer controlled_buffer_1
  assign Mem_to_Reg_out = IBI_Flags[5] ? MDR_p5 : 32'bz;  // Controlled_Buffer controlled_buffer_2
  assign MDR_p4 = IBRead ? Mem_to_Reg_in : 32'bz;  // Controlled_Buffer controlled_buffer_3
  assign Reg_to_Mem_out = IBWrite ? MDR_p5 : 32'bz;  // Controlled_Buffer controlled_buffer_4
  // Reg32 MAR: pin names not known; wires that end beside it: IBI_Flags[0], IBI_Flags[1], Clk, MAR_in, MAR_out

  // Other names for the same wires on the sheet: MARCE = IBI_Flags[0]; MAROE = IBI_Flags[1]; MDRCE = IBI_Flags[2];
  //   MDROE = IBI_Flags[3]; MDRput = IBI_Flags[4]; MDRget = IBI_Flags[5]
endmodule

module Given_Components (
);

  wire alu_1_p4, alu_1_p5, alu_1_p6, alu_1_p7, alu_1_p8, and_1_out, and_2_out, ANOP, AOP, Clock, CLR, DR,
       IBRead, IBWrite, Inverted_Clock, nor_1_out, or_1_out, reg32_1_p4, reg32_1_p6, reg32_2_p4, RegLD,
       RegSEL, SXR, SYR, T1CE, T1OE, T2CE, T2OE;
  wire [3:0] controlled_buffer_1_out, Opr;
  wire [7:0] Current_State_q, multiplexer_1_out, NextState, opcode, rom_1_data;
  wire [12:0] NotUsedInPart1;
  wire [23:0] Instruction_Register_q;
  wire [31:0] InterconnectionAddressBus, InterconnectionDataBus, InternalDataBus;

  // Probe on opcode
  Button Press_to_Clear_Internal_Processor_State (.out(CLR));
  and and_1 (and_1_out, Current_State_q[0], Current_State_q[1], ~Current_State_q[2], ~Current_State_q[3], ~Current_State_q[4], ~Current_State_q[5], ~Current_State_q[6], ~Current_State_q[7]);  // AND_Gate
  Register #(.width(32)) Instruction_Register (.Q({opcode, Instruction_Register_q}));  // open: D, en, clk, clr
  ROM rom_1 (.addr(opcode), .data(rom_1_data), .sel(and_1_out));
  Multiplexer #(.width(8)) multiplexer_1 (
    .in0(NextState), .in1(rom_1_data), .out(multiplexer_1_out), .sel(and_1_out));  // open: en
  // Probe on multiplexer_1_out
  // Probe on reg32_1_p4
  assign controlled_buffer_1_out = SYR ? Instruction_Register_q[15:12] : 4'bz;  // Controlled_Buffer controlled_buffer_1
  Register Current_State (.D(multiplexer_1_out), .Q(Current_State_q), .clk(Clock), .clr(CLR));  // open: en
  // Reg32 reg32_1: pin names not known; wires that end beside it: Clock, InternalDataBus, T1CE, reg32_1_p4, T1OE, reg32_1_p6, CLR
  assign controlled_buffer_1_out = SXR ? Instruction_Register_q[19:16] : 4'bz;  // Controlled_Buffer controlled_buffer_2
  // Probe on reg32_1_p6
  Clock Testing_clock (.out(Clock));
  assign controlled_buffer_1_out = DR ? Instruction_Register_q[23:20] : 4'bz;  // Controlled_Buffer controlled_buffer_3
  assign Opr = AOP ? opcode[3:0] : 4'bz;  // Controlled_Buffer controlled_buffer_4
  assign Opr = ANOP ? 4'b0000 : 4'bz;  // Controlled_Buffer controlled_buffer_5
  ROM #(.dataWidth(32)) rom_2 (
    .addr(Current_State_q),
    .data({NotUsedInPart1, AOP, ANOP, DR, SXR, SYR, RegSEL, RegLD, T1CE, T1OE, T2CE, T2OE, NextState}));  // open: sel
  not not_1 (Inverted_Clock, Clock);
  // Probe on NextState
  // Probe on InternalDataBus
  // ALU alu_1: pin names not known; wires that end beside it: reg32_1_p6, InternalDataBus, Opr, alu_1_p4, alu_1_p5, alu_1_p6, alu_1_p7, alu_1_p8
  LED led_1 (.in(alu_1_p5));
  LED led_2 (.in(alu_1_p6));
  LED led_3 (.in(alu_1_p7));
  LED led_4 (.in(alu_1_p8));
  // Probe on alu_1_p4
  // Probe on controlled_buffer_1_out
  // Probe on reg32_2_p4
  // Reg32 reg32_2: pin names not known; wires that end beside it: Clock, alu_1_p4, T2CE, reg32_2_p4, T2OE, InternalDataBus, CLR
  RAM #(.addrWidth(4), .dataWidth(32)) ram_1 (
    .addr(controlled_buffer_1_out), .data(InternalDataBus), .sel(RegSEL), .clk(Inverted_Clock), .ld(RegLD),
    .clr(CLR));
  // Probe on InternalDataBus
  nor nor_1 (nor_1_out, InterconnectionAddressBus[6], InterconnectionAddressBus[7], InterconnectionAddressBus[8], InterconnectionAddressBus[9], InterconnectionAddressBus[10], InterconnectionAddressBus[11], InterconnectionAddressBus[12], InterconnectionAddressBus[13], InterconnectionAddressBus[14], InterconnectionAddressBus[15], InterconnectionAddressBus[16], InterconnectionAddressBus[17], InterconnectionAddressBus[18], InterconnectionAddressBus[19], InterconnectionAddressBus[20], InterconnectionAddressBus[21], InterconnectionAddressBus[22], InterconnectionAddressBus[23], InterconnectionAddressBus[24], InterconnectionAddressBus[25], InterconnectionAddressBus[26], InterconnectionAddressBus[27], InterconnectionAddressBus[28], InterconnectionAddressBus[29], InterconnectionAddressBus[30], InterconnectionAddressBus[31]);
  and and_2 (and_2_out, nor_1_out, or_1_out);
  or or_1 (or_1_out, IBWrite, IBRead);
  RAM #(.addrWidth(6), .dataWidth(32)) ram_2 (
    .addr(InterconnectionAddressBus[5:0]), .data(InterconnectionDataBus), .sel(and_2_out),
    .clk(Inverted_Clock), .ld(IBRead));  // open: clr

  // Notes on the sheet:
  //   Decode ROM
  //   Use opcode to pick next state during decode state
  //   (Does not clear ROM contents)
  //   For each instruction, this ROM holds the next state that follows the Decode State.
  //   This design requies that Decode state is state  0x03
  //   Control FSM
  //   upper 4 bits of opcode
  //   not used in this lab
  //   next state from Output ROM
  //   Control FSM Outputs
  //   (Poke to toggle)
  //   Invert for latching if needed
  //   Register Address Bus
  //   16 x 32-bit Register Bank
  //   in Part 2 ONLY!
  //   Use this Main Memory component 
endmodule

module RAM_test (
  input  [3:0] in_1,
  input  RegLD_RegR,
  input  [31:0] in_3,
  input  RegSEL_RegW,
  output [31:0] out_5
);

  wire clock_1_out, not_1_out;
  wire [31:0] controlled_buffer_1_out;

  Clock clock_1 (.out(clock_1_out));
  RAM #(.addrWidth(4), .dataWidth(32)) ram_1 (
    .addr(in_1), .data(out_5), .sel(RegSEL_RegW), .clk(clock_1_out), .ld(RegLD_RegR));  // open: clr
  assign controlled_buffer_1_out = not_1_out ? in_3 : 32'bz;  // Controlled_Buffer controlled_buffer_1
  not not_1 (not_1_out, RegLD_RegR);
endmodule
