// Logisim project Lab6.circ as structural Verilog: 1 circuit, main circuit main
module main (
);

  wire AADD, alu_1_p4, alu_1_p5, alu_1_p6, alu_1_p7, alu_1_p8, and_1_out, and_2_out, ANOP, AOP, C1OE, Clock,
       CLR, DR, IBRead, IBWrite, Inverted_Clock, IRCE, IRS16, IRS20, IRU16, IRU20, MARCE, MAROE, MDRCE,
       MDRget, MDROE, MDRput, nor_1_out, or_1_out, PCOE, reg32_1_p4, reg32_1_p6, reg32_2_p4, reg32_3_p4,
       reg32_4_p4, RegLD, RegSEL, SXR, SYR, T1CE, T1OE, T2CE, T2OE, Unused;
  wire [3:0] controlled_buffer_1_out, Opr;
  wire [7:0] Current_State_q, multiplexer_1_out, NextState, opcode, rom_1_data;
  wire [15:0] IR16;
  wire [19:16] IR20;
  wire [23:20] Instruction_Register_q;
  wire [31:0] controlled_buffer_13_out, InterconnectionAddressBus, InterconnectionDataBus, InternalDataBus,
       reg32_3_p6;

  // Probe on opcode
  Button Clear_Internal_State (.out(CLR));
  and and_1 (and_1_out, Current_State_q[0], Current_State_q[1], ~Current_State_q[2], ~Current_State_q[3], ~Current_State_q[4], ~Current_State_q[5], ~Current_State_q[6], ~Current_State_q[7]);  // AND_Gate
  Register #(.width(32)) Instruction_Register (
    .D(InternalDataBus), .en(IRCE), .Q({opcode, Instruction_Register_q, IR20, IR16}), .clk(Inverted_Clock),
    .clr(CLR));
  ROM rom_1 (.addr(opcode), .data(rom_1_data), .sel(and_1_out));
  Multiplexer #(.width(8)) multiplexer_1 (
    .in0(NextState), .in1(rom_1_data), .out(multiplexer_1_out), .sel(and_1_out));  // open: en
  // Probe on multiplexer_1_out
  // Probe on reg32_1_p4
  assign controlled_buffer_1_out = SYR ? IR16[15:12] : 4'bz;  // Controlled_Buffer controlled_buffer_1
  assign InternalDataBus = IRU16 ? {{16{1'b0}}, IR16} : 32'bz;  // Controlled_Buffer controlled_buffer_2
  assign InternalDataBus = IRU20 ? {{12{1'b0}}, IR20, IR16} : 32'bz;  // Controlled_Buffer controlled_buffer_3
  Register Current_State (.D(multiplexer_1_out), .Q(Current_State_q), .clk(Clock), .clr(CLR));  // open: en
  // Reg32 reg32_1: pin names not known; wires that end beside it: Clock, InternalDataBus, T1CE, reg32_1_p4, T1OE, reg32_1_p6, CLR
  assign controlled_buffer_1_out = SXR ? IR20 : 4'bz;  // Controlled_Buffer controlled_buffer_4
  // Probe on reg32_1_p6
  // Probe on InternalDataBus
  // Probe on Opr
  Clock Testing_clock (.out(Clock));
  assign controlled_buffer_1_out = DR ? Instruction_Register_q : 4'bz;  // Controlled_Buffer controlled_buffer_5
  assign Opr = AOP ? opcode[3:0] : 4'bz;  // Controlled_Buffer controlled_buffer_6
  assign Opr = ANOP ? 4'b0000 : 4'bz;  // Controlled_Buffer controlled_buffer_7
  ROM #(.dataWidth(32)) rom_2 (
    .addr(Current_State_q),
    .data({Unused, IRCE, PCOE, C1OE, AADD, MARCE, MAROE, MDRCE, MDROE, MDRget, MDRput, IBRead, IBWrite, AOP, ANOP, DR, SXR, SYR, RegSEL, RegLD, T1CE, T1OE, T2CE, T2OE, NextState}));  // open: sel
  ROM #(.dataWidth(4)) rom_3 (.addr(Current_State_q), .data({IRS20, IRS16, IRU20, IRU16}));  // open: sel
  not not_1 (Inverted_Clock, Clock);
  assign Opr = AADD ? 4'b0001 : 4'bz;  // Controlled_Buffer controlled_buffer_8
  // Probe on NextState
  // Probe on InternalDataBus
  // ALU alu_1: pin names not known; wires that end beside it: reg32_1_p6, InternalDataBus, Opr, alu_1_p4, alu_1_p5, alu_1_p6, alu_1_p7, alu_1_p8
  LED led_1 (.in(alu_1_p5));
  LED led_2 (.in(alu_1_p6));
  LED led_3 (.in(alu_1_p7));
  LED led_4 (.in(alu_1_p8));
  assign controlled_buffer_1_out = PCOE ? 4'b1111 : 4'bz;  // Controlled_Buffer controlled_buffer_9
  // Probe on alu_1_p4
  // Probe on controlled_buffer_1_out
  // Probe on reg32_2_p4
  // Reg32 reg32_2: pin names not known; wires that end beside it: Clock, alu_1_p4, T2CE, reg32_2_p4, T2OE, InternalDataBus, CLR
  // Probe on InternalDataBus
  RAM #(.addrWidth(4), .dataWidth(32)) ram_1 (
    .addr(controlled_buffer_1_out), .data(InternalDataBus), .sel(RegSEL), .clk(Inverted_Clock), .ld(RegLD),
    .clr(CLR));
  assign InternalDataBus = C1OE ? 32'h1 : 32'bz;  // Controlled_Buffer controlled_buffer_10
  assign InternalDataBus = IRS16 ? {{17{IR16[15]}}, IR16[14:0]} : 32'bz;  // Controlled_Buffer controlled_buffer_11
  assign InternalDataBus = IRS20 ? {{13{IR20[19]}}, IR20[18:16], IR16} : 32'bz;  // Controlled_Buffer controlled_buffer_12
  assign controlled_buffer_13_out = MDRput ? InternalDataBus : 32'bz;  // Controlled_Buffer controlled_buffer_13
  assign controlled_buffer_13_out = IBRead ? InterconnectionDataBus : 32'bz;  // Controlled_Buffer controlled_buffer_14
  // Probe on reg32_3_p4
  // Reg32 reg32_3: pin names not known; wires that end beside it: Clock, controlled_buffer_13_out, MDRCE, reg32_3_p4, MDROE, reg32_3_p6, CLR
  nor nor_1 (nor_1_out, InterconnectionAddressBus[6], InterconnectionAddressBus[7], InterconnectionAddressBus[8], InterconnectionAddressBus[9], InterconnectionAddressBus[10], InterconnectionAddressBus[11], InterconnectionAddressBus[12], InterconnectionAddressBus[13], InterconnectionAddressBus[14], InterconnectionAddressBus[15], InterconnectionAddressBus[16], InterconnectionAddressBus[17], InterconnectionAddressBus[18], InterconnectionAddressBus[19], InterconnectionAddressBus[20], InterconnectionAddressBus[21], InterconnectionAddressBus[22], InterconnectionAddressBus[23], InterconnectionAddressBus[24], InterconnectionAddressBus[25], InterconnectionAddressBus[26], InterconnectionAddressBus[27], InterconnectionAddressBus[28], InterconnectionAddressBus[29], InterconnectionAddressBus[30], InterconnectionAddressBus[31]);
  assign InternalDataBus = MDRget ? reg32_3_p6 : 32'bz;  // Controlled_Buffer controlled_buffer_15
  assign InterconnectionDataBus = IBWrite ? reg32_3_p6 : 32'bz;  // Controlled_Buffer controlled_buffer_16
  and and_2 (and_2_out, nor_1_out, or_1_out);
  or or_1 (or_1_out, IBWrite, IBRead);
  // Probe on reg32_4_p4
  // Reg32 reg32_4: pin names not known; wires that end beside it: Clock, InternalDataBus, MARCE, reg32_4_p4, MAROE, InterconnectionAddressBus, CLR
  RAM #(.addrWidth(6), .dataWidth(32)) ram_2 (
    .addr(InterconnectionAddressBus[5:0]), .data(InterconnectionDataBus), .sel(and_2_out),
    .clk(Inverted_Clock), .ld(IBRead));  // open: clr

  // Other names for the same wires on the sheet: IR20[15:0] = IR16

  // Notes on the sheet:
  //   Decode ROM
  //   ROM holds next state for each operation (after decode state)
  //   Use opcode to pick next state during decode state
  //   This design requies that Decode state is state  0x03
  //   Constant 0
  //   Control FSM
  //   next state from ROM
  //   Control FSM (LO ROM)
  //   Control FSM (HI ROM)
  //   (Poke to toggle)
  //   Invert for latching if needed
  //   signals for immediate data 
  //   onto Internal Data Bus
  //   Register Address Bus
  //   16 x 32-bit Register Bank
  //   Interconnect Bus Interface
  //   Main Memory component 
endmodule
